// Logisim project fetch.circ as structural Verilog: 1 circuit, main circuit main
module main (
  input  in_1,
  input  in_2,
  input  in_3,
  output [31:0] out_4,
  output [31:0] out_5
);

  wire [31:0] adder_1_out;

  Register #(.width(32)) register_1 (.D(adder_1_out), .Q(out_4), .clk(in_1), .clr(in_2));  // open: en
  Adder #(.width(32)) adder_1 (.a(32'h4), .b(out_4), .out(adder_1_out));  // open: cin, cout
  ROM #(.addrWidth(16), .dataWidth(32)) rom_1 (.addr(out_4[15:0]), .data(out_5), .sel(in_3));
endmodule
